# Fritzing sketch RealFakeGarageDoors (saved by Fritzing 0.9.3b)
breadboards: 1

parts:
  Q2 = NPN-Transistor [package="TO92 [THT]"]
  Q1 = NPN-Transistor [package="TO92 [THT]"]
  R2 = Resistor [tolerance=±5% resistance=10k package="0805 [SMD]"]
  Multi-code_Remote = mystery part, 4 pins [chip_label="Multi-code Remote"]
  R1 = Resistor [tolerance=±5% resistance=10k package="0805 [SMD]"]
  U1 = NodeMCU

nets (from the schematic view):
  GND: Q2.E, Q1.E, Multi-code_Remote.pin3, Multi-code_Remote.pin4, U1.connector13
  N1: Q2.B, R2.Pin_1
  N2: Q2.C, Multi-code_Remote.pin1
  N3: Q1.B, R1.Pin_1
  N4: Q1.C, Multi-code_Remote.pin2
  N5: R2.Pin_0, U1.connector1
  N6: R1.Pin_0, U1.connector7

notes:
  Multi-code Remote
  Real Fake Garage Doors
